# Fritzing sketch BlinkingLeds (saved by Fritzing 0.9.2b)
breadboards: 1

parts:
  LED0 = LED - 5mm [color="Red (633nm)" package="5 mm [THT]"]
  LED1 = LED - 5mm [color="Red (633nm)" package="5 mm [THT]"]
  LED2 = LED - 5mm [color="Red (633nm)" package="5 mm [THT]"]
  LED3 = LED - 5mm [color="Red (633nm)" package="5 mm [THT]"]
  LED4 = LED - 5mm [color="Red (633nm)" package="5 mm [THT]"]
  R0 = Resistor [tolerance=±5% resistance=220 package=THT]
  R2 = Resistor [tolerance=±5% resistance=220 package=THT]
  R3 = Resistor [tolerance=±5% resistance=220 package=THT]
  R4 = Resistor [tolerance=±5% resistance=220 package=THT]
  R1 = Resistor [tolerance=±5% resistance=220 package=THT]
  S1 = Pushbutton [package="[THT]"]
  R7 = Resistor [tolerance=±5% resistance=220 package=THT]
  BlinkingLEDs = Arduino Uno (Rev3)

nets:
  N1: LED0.cathode, R0.Pin_0
  N2: LED0.anode, BlinkingLEDs.D2
  N3: LED1.cathode, R1.Pin_0
  N4: LED1.anode, BlinkingLEDs.D3_PWM
  N5: LED2.cathode, R2.Pin_0
  N6: LED2.anode, BlinkingLEDs.D4
  N7: LED3.cathode, R3.Pin_0
  N8: LED3.anode, BlinkingLEDs.D5_PWM
  N9: LED4.cathode, R4.Pin_0
  N10: LED4.anode, BlinkingLEDs.D6_PWM
  N11: R0.Pin_1, R2.Pin_1, R3.Pin_1, R4.Pin_1, R1.Pin_1, R7.Pin_1, BlinkingLEDs.GND
  N12: S1.Pin_2, R7.Pin_0, BlinkingLEDs.D7
  N13: S1.Pin_4, BlinkingLEDs.5V

notes:
  D2
  D3
  D4
  D5
  D6
  2
  0
  1
  3
  4
